# Fritzing sketch envduino (saved by Fritzing 0.6.3b)
breadboards: 1

parts:
  Arduino1 = Arduino
  DHT1 = DHT22_Humidity_and_Temperature_Sensor
  R1 = Resistor [tolerance=±5% resistance=10k package=THT]

nets:
  GND: Arduino1.GND, DHT1.connector4
  N1: Arduino1.D11, DHT1.connector2, R1.Pin_0
  N2: Arduino1.3V3, DHT1.connector1, R1.Pin_1
