# Fritzing sketch envduino (saved by Fritzing 0.8.0b)
breadboards: 2

parts:
  BMP1 = BMP085 Breakout
  U1 = Arduino Mega
  LED1 = LED - 5mm [color="Yellow (592nm)" package="5 mm [THT]"]
  LED2 = LED - 5mm [color="Red (633nm)" package="5 mm [THT]"]
  LED3 = LED - 5mm [color="Green (560nm)" package="5 mm [THT]"]
  R2 = Resistor [tolerance=±5% resistance=330 package=THT]
  R1 = Resistor [tolerance=±5% resistance=330 package=THT]
  R3 = Resistor [tolerance=±5% resistance=330 package=THT]
  DHT1 = DHT22 Humidity and Temperature Sensor
  R4 = Resistor [tolerance=±5% resistance=10k package=THT]

nets:
  N1: BMP1.3Vo, U1.3V3
  N2: BMP1.SCL, U1.D21
  N3: BMP1.SDA, U1.D20
  GND: BMP1.GND, U1.GND, R2.Pin_1, R1.Pin_1, R3.Pin_1, DHT1.GND
  +5V: U1.+5V, DHT1.VDD, R4.Pin_1
  N4: U1.D22, LED3.cathode
  N5: U1.D24, LED1.cathode
  N6: U1.D26, LED2.cathode
  N7: U1.D28, DHT1.DATA, R4.Pin_0
  N8: LED1.anode, R1.Pin_0
  N9: LED2.anode, R2.Pin_0
  N10: LED3.anode, R3.Pin_0

custom parts:
  BMP085 Breakout: A breakout for the BMP085 barometric pressure and temperature sensor
